# Fritzing sketch Project-1 (saved by Fritzing 0.9.3b)
breadboards: 1

parts:
  Part1 = Arduino Uno (Rev3)
  R1 = Photocell (LDR) [package=THT]
  R2 = Resistor [tolerance=±5% resistance=220 package=THT]
  R3 = Resistor [tolerance=±5% resistance=10k package=THT]
  LED1 = LED - 5mm [color="Yellow (595nm)" package="5 mm [THT]"]
  hc-sr1 = hc-sr04

nets:
  N1: Part1.A0, R1.pin_1, R3.Pin_0
  N2: Part1.D13/SCK, R2.Pin_1
  N3: Part1.D2, hc-sr1.Trig
  N4: Part1.D3_PWM, hc-sr1.Echo
  5V: Part1.5V, R1.pin_0, hc-sr1.VCC
  GND: Part1.GND, R3.Pin_1, LED1.cathode, hc-sr1.GND
  N5: R2.Pin_0, LED1.anode
